// Logisim project ex4.circ as structural Verilog: 5 circuits, main circuit RotRight
module RotRight (
  input  [15:0] INPUT0,
  input  [3:0] AMOUNT,
  output [15:0] OUTPUT0
);

  wire [15:0] multiplexer_1_out, multiplexer_2_out, multiplexer_3_out, R1, R2, R4, R8;

  Multiplexer #(.width(16)) multiplexer_1 (.in0(INPUT0), .in1(R8), .out(multiplexer_1_out), .sel(AMOUNT[3]));
  rot1 rot1_1 (.out_2(R1), .in_1(multiplexer_3_out));
  rot2 rot2_1 (.out_2(R2), .in_1(multiplexer_2_out));
  rot4 rot4_1 (.out_2(R4), .in_1(multiplexer_1_out));
  rot8 rot8_1 (.out_2(R8), .in_1(INPUT0));
  Multiplexer #(.width(16)) multiplexer_2 (.in0(multiplexer_1_out), .in1(R4), .out(multiplexer_2_out), .sel(AMOUNT[2]));
  Multiplexer #(.width(16)) multiplexer_3 (.in0(multiplexer_2_out), .in1(R2), .out(multiplexer_3_out), .sel(AMOUNT[1]));
  Multiplexer #(.width(16)) multiplexer_4 (.in0(multiplexer_3_out), .in1(R1), .out(OUTPUT0), .sel(AMOUNT[0]));
endmodule

module rot1 (
  input  [15:0] in_1,
  output [15:0] out_2
);


  assign out_2 = {in_1[0], in_1[15:1]};
endmodule

module rot2 (
  input  [15:0] in_1,
  output [15:0] out_2
);


  assign out_2 = {in_1[1:0], in_1[15:2]};
endmodule

module rot4 (
  input  [15:0] in_1,
  output [15:0] out_2
);


  assign out_2 = {in_1[3:0], in_1[15:4]};
endmodule

module rot8 (
  input  [15:0] in_1,
  output [15:0] out_2
);


  assign out_2 = {in_1[7:0], in_1[15:8]};
endmodule
