// Logisim project control-logic.circ as structural Verilog: 1 circuit, main circuit control_logic
module control_logic (
  input  [31:0] Instruction,
  input  BrEq,
  input  BrLt,
  output PCSel,
  output RegWEn,
  output [2:0] ImmSel,
  output BrUn,
  output ASel,
  output BSel,
  output [3:0] ALUSel,
  output MemWEn,
  output [1:0] WBSel,
  output [5:0] out_13
);

  wire and_13_out, and_14_out, and_15_out, and_16_out, and_17_out, and_18_out, B_type, comparator_1_eq,
       comparator_2_eq, comparator_3_eq, comparator_4_eq, comparator_5_eq, comparator_6_eq, comparator_16_eq,
       comparator_17_eq, comparator_18_eq, comparator_19_eq, comparator_20_eq, comparator_21_eq,
       comparator_30_eq, comparator_31_eq, comparator_32_eq, Func3_0, Func3_1, Func3_2, Func3_3, Func3_4,
       Func3_5, Func3_6, Func3_7, I_1_type, I_2_type, I_3_type, In0, In1, In2, In3, In4, In5, In6, In7, In8,
       In9, In10, In11, In12, In13, In14, In15, In16, In17, In18, In19, In20, In22, In23, In24, In25, In26,
       In27, In28, In29, In30, In31, In32, In33, In34, In35, not_1_out, not_2_out, not_3_out, R_type, S_type;
  wire [15:14] rom_1_data;

  ROM #(.addrWidth(6), .dataWidth(16)) rom_1 (
    .addr(out_13), .data({rom_1_data, WBSel, MemWEn, ALUSel, BSel, ASel, BrUn, ImmSel, RegWEn}));
  Comparator #(.mode("unsigned"), .width(7)) comparator_1 (
    .a(Instruction[31:25]), .b({7{1'b0}}), .eq(comparator_1_eq));  // open: gt, lt
  Comparator #(.mode("unsigned"), .width(7)) comparator_2 (
    .a(Instruction[31:25]), .b(7'b0000001), .eq(comparator_2_eq));  // open: gt, lt
  Comparator #(.mode("unsigned"), .width(7)) comparator_3 (
    .a(Instruction[31:25]), .b(7'b0100000), .eq(comparator_3_eq));  // open: gt, lt
  Comparator #(.mode("unsigned"), .width(7)) comparator_4 (
    .a(Instruction[31:25]), .b({7{1'b0}}), .eq(comparator_4_eq));  // open: gt, lt
  Comparator #(.mode("unsigned"), .width(7)) comparator_5 (
    .a(Instruction[31:25]), .b(7'b0000001), .eq(comparator_5_eq));  // open: gt, lt
  Comparator #(.mode("unsigned"), .width(7)) comparator_6 (
    .a(Instruction[31:25]), .b(7'b0000001), .eq(comparator_6_eq));  // open: gt, lt
  and and_1 (In0, R_type, comparator_1_eq, Func3_0);
  and and_2 (In1, R_type, comparator_2_eq, Func3_0);
  and and_3 (In2, R_type, comparator_3_eq, Func3_0);
  and and_4 (In3, R_type, comparator_4_eq, Func3_1);
  and and_5 (In4, R_type, comparator_5_eq, Func3_1);
  and and_6 (In5, R_type, comparator_6_eq, Func3_3);
  Comparator #(.mode("unsigned"), .width(7)) comparator_7 (
    .a(Instruction[6:0]), .b(7'b0110011), .eq(R_type));  // open: gt, lt
  Comparator #(.mode("unsigned"), .width(7)) comparator_8 (
    .a(Instruction[6:0]), .b(7'b0000011), .eq(I_1_type));  // open: gt, lt
  Comparator #(.mode("unsigned"), .width(7)) comparator_9 (
    .a(Instruction[6:0]), .b(7'b0010011), .eq(I_2_type));  // open: gt, lt
  Comparator #(.mode("unsigned"), .width(7)) comparator_10 (
    .a(Instruction[6:0]), .b(7'b0100011), .eq(S_type));  // open: gt, lt
  Comparator #(.mode("unsigned"), .width(7)) comparator_11 (
    .a(Instruction[6:0]), .b(7'b1100011), .eq(B_type));  // open: gt, lt
  Comparator #(.mode("unsigned"), .width(7)) comparator_12 (
    .a(Instruction[6:0]), .b(7'b0010111), .eq(In32));  // open: gt, lt
  Comparator #(.mode("unsigned"), .width(7)) comparator_13 (
    .a(Instruction[6:0]), .b(7'b0110111), .eq(In33));  // open: gt, lt
  Comparator #(.mode("unsigned"), .width(7)) comparator_14 (
    .a(Instruction[6:0]), .b(7'b1101111), .eq(In34));  // open: gt, lt
  Comparator #(.mode("unsigned"), .width(7)) comparator_15 (
    .a(Instruction[6:0]), .b(7'b1100111), .eq(I_3_type));  // open: gt, lt
  Comparator #(.mode("unsigned"), .width(7)) comparator_16 (
    .a(Instruction[31:25]), .b({7{1'b0}}), .eq(comparator_16_eq));  // open: gt, lt
  Comparator #(.mode("unsigned"), .width(7)) comparator_17 (
    .a(Instruction[31:25]), .b({7{1'b0}}), .eq(comparator_17_eq));  // open: gt, lt
  Comparator #(.mode("unsigned"), .width(7)) comparator_18 (
    .a(Instruction[31:25]), .b({7{1'b0}}), .eq(comparator_18_eq));  // open: gt, lt
  Comparator #(.mode("unsigned"), .width(7)) comparator_19 (
    .a(Instruction[31:25]), .b(7'b0100000), .eq(comparator_19_eq));  // open: gt, lt
  Comparator #(.mode("unsigned"), .width(7)) comparator_20 (
    .a(Instruction[31:25]), .b({7{1'b0}}), .eq(comparator_20_eq));  // open: gt, lt
  Comparator #(.mode("unsigned"), .width(7)) comparator_21 (
    .a(Instruction[31:25]), .b({7{1'b0}}), .eq(comparator_21_eq));  // open: gt, lt
  and and_7 (In6, R_type, comparator_16_eq, Func3_2);
  and and_8 (In7, R_type, comparator_17_eq, Func3_4);
  and and_9 (In8, R_type, comparator_18_eq, Func3_5);
  and and_10 (In9, R_type, comparator_19_eq, Func3_5);
  and and_11 (In10, R_type, comparator_20_eq, Func3_6);
  and and_12 (In11, R_type, comparator_21_eq, Func3_7);
  Comparator #(.mode("unsigned"), .width(3)) comparator_22 (
    .a(Instruction[14:12]), .b(3'b000), .eq(Func3_0));  // open: gt, lt
  Comparator #(.mode("unsigned"), .width(3)) comparator_23 (
    .a(Instruction[14:12]), .b(3'b001), .eq(Func3_1));  // open: gt, lt
  Comparator #(.mode("unsigned"), .width(3)) comparator_24 (
    .a(Instruction[14:12]), .b(3'b010), .eq(Func3_2));  // open: gt, lt
  Comparator #(.mode("unsigned"), .width(3)) comparator_25 (
    .a(Instruction[14:12]), .b(3'b011), .eq(Func3_3));  // open: gt, lt
  Comparator #(.mode("unsigned"), .width(3)) comparator_26 (
    .a(Instruction[14:12]), .b(3'b100), .eq(Func3_4));  // open: gt, lt
  Comparator #(.mode("unsigned"), .width(3)) comparator_27 (
    .a(Instruction[14:12]), .b(3'b101), .eq(Func3_5));  // open: gt, lt
  Comparator #(.mode("unsigned"), .width(3)) comparator_28 (
    .a(Instruction[14:12]), .b(3'b110), .eq(Func3_6));  // open: gt, lt
  Comparator #(.mode("unsigned"), .width(3)) comparator_29 (
    .a(Instruction[14:12]), .b(3'b111), .eq(Func3_7));  // open: gt, lt
  not not_1 (not_1_out, BrEq);
  not not_2 (not_2_out, BrLt);
  not not_3 (not_3_out, BrLt);
  Comparator #(.mode("unsigned"), .width(7)) comparator_30 (
    .a(Instruction[31:25]), .b({7{1'b0}}), .eq(comparator_30_eq));  // open: gt, lt
  and and_13 (and_13_out, In26, BrEq);
  and and_14 (and_14_out, In27, not_1_out);
  and and_15 (and_15_out, In28, BrLt);
  and and_16 (and_16_out, In29, not_2_out);
  and and_17 (and_17_out, In30, BrLt);
  and and_18 (and_18_out, In31, not_3_out);
  and and_19 (In12, I_1_type, Func3_0);
  and and_20 (In13, I_1_type, Func3_1);
  and and_21 (In14, I_1_type, Func3_2);
  and and_22 (In15, I_2_type, Func3_0);
  and and_23 (In16, I_2_type, comparator_30_eq, Func3_1);
  and and_24 (In17, I_2_type, Func3_2);
  or or_1 (PCSel, and_13_out, and_14_out, and_15_out, and_16_out, and_17_out, and_18_out, In34, In35);
  Comparator #(.mode("unsigned"), .width(7)) comparator_31 (
    .a(Instruction[31:25]), .b({7{1'b0}}), .eq(comparator_31_eq));  // open: gt, lt
  Comparator #(.mode("unsigned"), .width(7)) comparator_32 (
    .a(Instruction[31:25]), .b(7'b0100000), .eq(comparator_32_eq));  // open: gt, lt
  and and_25 (In18, I_2_type, Func3_4);
  and and_26 (In19, I_2_type, comparator_31_eq, Func3_5);
  and and_27 (In20, I_2_type, comparator_32_eq, Func3_5);
  and and_28 (In20, I_2_type, Func3_6);
  and and_29 (In22, I_2_type, Func3_7);
  and and_30 (In23, S_type, Func3_0);
  Priority_Encoder #(.select_enc(6)) priority_encoder_1 (
    .in0(In0), .in1(In1), .in2(In2), .in3(In3), .in4(In4), .in5(In5), .in6(In6), .in7(In7), .in8(In8),
    .in9(In9), .in10(In10), .in11(In11), .in12(In12), .in13(In13), .in14(In14), .in15(In15), .in16(In16),
    .in17(In17), .in18(In18), .in19(In19), .in20(In20), .in21(In20), .in22(In22), .in23(In23), .in24(In24),
    .in25(In25), .in26(In26), .in27(In27), .in28(In28), .in29(In29), .in30(In30), .in31(In31), .in32(In32),
    .in33(In33), .in34(In34), .in35(In35), .out(out_13));  // open: in36, in37, in38, in39, in40, in41, in42, in43, in44, in45, in46, in47, in48, in49, in50, in51, in52, in53, in54, in55, in56, in57, in58, in59, in60, in61, in62, in63, gs, en_out, en_in
  and and_31 (In24, S_type, Func3_1);
  and and_32 (In25, S_type, Func3_2);
  and and_33 (In26, B_type, Func3_0);
  and and_34 (In27, B_type, Func3_1);
  and and_35 (In28, B_type, Func3_4);
  and and_36 (In29, B_type, Func3_5);
  and and_37 (In30, B_type, Func3_6);
  and and_38 (In31, B_type, Func3_7);
  and and_39 (In35, I_3_type, Func3_0);

  // Other names for the same wires on the sheet: In21 = In20; opcode[6:0] = Instruction[6:0];
  //   funct3[2:0] = Instruction[14:12]; funct7[6:0] = Instruction[31:25]; J_type = In34; ROM_Input[5:0] = out_13;
  //   U_1_type = In32; U_2_type = In33

  // Notes on the sheet:
  //   INPUTS to your circuit
  //   Connect ROM Input here ->
  //   contents of rom_1 (hex, n*v repeats v):
  //   1001 1401 1601 1081 1481 1581 1101 1201 1281 1681 1301 1381 41 41 41 1041 10c1 1141 1241 12c1 16c1
  //   1341 13c1 842 842 842 4*1065 1075 1075 1067 17e7 2069 2041
  //   ROM FOR CONTROL LOGIC
  //   DON'T CHANGE THE LOCATIONS OF THE INPUTS AND OUTPUTS!
  //   This is only if you choose to do the ROM option
  //   CONNECT
  //   WIRE
  //   TO
  //   USE
  //   ROM
  //   OUTPUT from your circuit
  //   Reminder: If using ROM, use combinational logic for PCSel
endmodule
