// Logisim project imm-gen.circ as structural Verilog: 1 circuit, main circuit imm_gen
module imm_gen (
  input  [31:0] Instruction,
  input  [2:0] ImmSel,
  output [31:0] Immediate
);

  wire [11:0] Bits31_20;
  wire [19:0] Bits31_12;
  wire [20:0] Bits31_11;

  assign Bits31_20 = {{11{Instruction[31]}}, Instruction[31]};  // Bit_Extender bit_extender_1
  assign Bits31_12 = {{19{Instruction[31]}}, Instruction[31]};  // Bit_Extender bit_extender_2
  assign Bits31_11 = {{20{Instruction[31]}}, Instruction[31]};  // Bit_Extender bit_extender_3
  Multiplexer #(.select(3), .width(32)) multiplexer_1 (
    .in0({Bits31_11, Instruction[30:20]}), .in1({Bits31_11, Instruction[30:25], Instruction[11:7]}),
    .in2({Bits31_12, Instruction[7], Instruction[30:25], Instruction[11:8], 1'b0}),
    .in3({Instruction[31:12], {12{1'b0}}}),
    .in4({Bits31_20, Instruction[19:12], Instruction[20], Instruction[30:21], 1'b0}), .out(Immediate),
    .sel(ImmSel));  // open: in5, in6, in7

  // Other names for the same wires on the sheet: ImmeB_2[31:1] = {Bits31_12, Instruction[7], Instruction[30:25], Instruction[11:8]};
  //   ImmeJ_4[31:1] = {Bits31_20, Instruction[19:12], Instruction[20], Instruction[30:21]};
  //   ImmeI_0[31:0] = {Bits31_11, Instruction[30:20]};
  //   ImmeS_1[31:0] = {Bits31_11, Instruction[30:25], Instruction[11:7]}; Inst7 = Instruction[7];
  //   Inst11_8[3:0] = Instruction[11:8]; ImmeU_3[31:12] = Instruction[31:12]; Inst19_12[7:0] = Instruction[19:12];
  //   Inst20 = Instruction[20]; Inst24_21[3:0] = Instruction[24:21]; Inst30_25[5:0] = Instruction[30:25];
  //   Inst31 = Instruction[31]

  // Notes on the sheet:
  //   INPUTS to your circuit
  //   DON'T CHANGE THE LOCATIONS OF THE INPUTS AND OUTPUTS!
  //   OUTPUT from your circuit
endmodule
