// Logisim project partial-load.circ as structural Verilog: 1 circuit, main circuit partial_load
module partial_load (
  input  [31:0] Instruction,
  input  [31:0] MemAddress,
  input  [31:0] DataFromMem,
  output [31:0] DataToReg
);

  wire bot_0, bot_1, bot_2, bot_3, f3_0, f3_1, f3_2, lb_0, lb_1, lb_2, lb_3, lh_0, lh_1, lh_2, lw, op_3;
  wire [2:0] DataSel;
  wire [31:0] Data7_0, Data15_0, Data15_8, Data23_8, Data23_16, Data31_16, Data31_24;

  Comparator #(.mode("unsigned"), .width(7)) comparator_1 (
    .a(Instruction[6:0]), .b(7'b0000011), .eq(op_3));  // open: gt, lt
  Comparator #(.mode("unsigned"), .width(3)) comparator_2 (
    .a(Instruction[14:12]), .b(3'b000), .eq(f3_0));  // open: gt, lt
  Comparator #(.mode("unsigned"), .width(3)) comparator_3 (
    .a(Instruction[14:12]), .b(3'b001), .eq(f3_1));  // open: gt, lt
  Comparator #(.mode("unsigned"), .width(3)) comparator_4 (
    .a(Instruction[14:12]), .b(3'b010), .eq(f3_2));  // open: gt, lt
  assign Data7_0 = {{24{DataFromMem[7]}}, DataFromMem[7:0]};  // Bit_Extender bit_extender_1
  assign Data15_8 = {{24{DataFromMem[15]}}, DataFromMem[15:8]};  // Bit_Extender bit_extender_2
  assign Data23_16 = {{24{DataFromMem[23]}}, DataFromMem[23:16]};  // Bit_Extender bit_extender_3
  assign Data31_24 = {{24{DataFromMem[31]}}, DataFromMem[31:24]};  // Bit_Extender bit_extender_4
  Comparator #(.mode("unsigned"), .width(2)) comparator_5 (.a(MemAddress[1:0]), .b(2'b00), .eq(bot_0));  // open: gt, lt
  Comparator #(.mode("unsigned"), .width(2)) comparator_6 (.a(MemAddress[1:0]), .b(2'b01), .eq(bot_1));  // open: gt, lt
  Comparator #(.mode("unsigned"), .width(2)) comparator_7 (.a(MemAddress[1:0]), .b(2'b10), .eq(bot_2));  // open: gt, lt
  Comparator #(.mode("unsigned"), .width(2)) comparator_8 (.a(MemAddress[1:0]), .b(2'b11), .eq(bot_3));  // open: gt, lt
  Priority_Encoder priority_encoder_1 (
    .in0(lb_0), .in1(lb_1), .in2(lb_2), .in3(lb_3), .in4(lh_0), .in5(lh_1), .in6(lh_2), .in7(lw),
    .out(DataSel));  // open: en_in, gs, en_out
  assign Data15_0 = {{16{DataFromMem[15]}}, DataFromMem[15:0]};  // Bit_Extender bit_extender_5
  assign Data23_8 = {{16{DataFromMem[23]}}, DataFromMem[23:8]};  // Bit_Extender bit_extender_6
  assign Data31_16 = {{16{DataFromMem[31]}}, DataFromMem[31:16]};  // Bit_Extender bit_extender_7
  Multiplexer #(.select(3), .width(32)) multiplexer_1 (
    .in0(Data7_0), .in1(Data15_8), .in2(Data23_16), .in3(Data31_24), .in4(Data15_0), .in5(Data23_8),
    .in6(Data31_16), .in7(DataFromMem), .out(DataToReg), .sel(DataSel));
  and and_1 (lb_0, op_3, f3_0, bot_0);
  and and_2 (lb_1, op_3, f3_0, bot_1);
  and and_3 (lb_2, op_3, f3_0, bot_2);
  and and_4 (lb_3, op_3, f3_0, bot_3);
  and and_5 (lh_0, op_3, f3_1, bot_0);
  and and_6 (lh_1, op_3, f3_1, bot_1);
  and and_7 (lh_2, op_3, f3_1, bot_2);
  and and_8 (lw, op_3, f3_2);

  // Other names for the same wires on the sheet: data_0[7:0] = DataFromMem[7:0]; data_1[7:0] = DataFromMem[15:8];
  //   data_2[7:0] = DataFromMem[23:16]; data_3[7:0] = DataFromMem[31:24]; opcode[6:0] = Instruction[6:0];
  //   funct3[2:0] = Instruction[14:12]; funct7[6:0] = Instruction[31:25]; BOT[1:0] = MemAddress[1:0]

  // Notes on the sheet:
  //   INPUTS to your circuit
  //   DON'T CHANGE THE LOCATIONS OF THE INPUTS AND OUTPUTS!
  //   OUTPUT from your circuit
endmodule
