// Logisim project partial-store.circ as structural Verilog: 1 circuit, main circuit partial_store
module partial_store (
  input  [31:0] Instruction,
  input  [31:0] MemAddress,
  input  [31:0] DataFromReg,
  input  MemWEn,
  output [3:0] MemWriteMask,
  output [31:0] DataToMem
);

  wire bot_0, bot_1, bot_2, bot_3, f3_0, f3_1, f3_2, op_23, sb_0, sb_1, sb_2, sb_3, sh_0, sh_1, sw;
  wire [2:0] DataSel;

  Comparator #(.mode("unsigned"), .width(7)) comparator_1 (
    .a(Instruction[6:0]), .b(7'b0100011), .eq(op_23));  // open: gt, lt
  Comparator #(.mode("unsigned"), .width(3)) comparator_2 (
    .a(Instruction[14:12]), .b(3'b000), .eq(f3_0));  // open: gt, lt
  Comparator #(.mode("unsigned"), .width(3)) comparator_3 (
    .a(Instruction[14:12]), .b(3'b001), .eq(f3_1));  // open: gt, lt
  Comparator #(.mode("unsigned"), .width(3)) comparator_4 (
    .a(Instruction[14:12]), .b(3'b010), .eq(f3_2));  // open: gt, lt
  Priority_Encoder priority_encoder_1 (
    .in0(sb_0), .in1(sb_1), .in2(sb_2), .in3(sb_3), .in4(sh_0), .in5(sh_1), .in6(sw), .out(DataSel));  // open: in7, en_in, gs, en_out
  Multiplexer #(.select(3), .width(32)) multiplexer_1 (
    .in0({{24{1'b0}}, DataFromReg[7:0]}), .in1({{16{1'b0}}, DataFromReg[7:0], {8{1'b0}}}),
    .in2({{8{1'b0}}, DataFromReg[7:0], {16{1'b0}}}), .in3({DataFromReg[7:0], {24{1'b0}}}),
    .in4({DataFromReg[15:0], DataFromReg[15:0]}), .in5({DataFromReg[15:0], DataFromReg[15:0]}),
    .in6(DataFromReg), .out(DataToMem), .sel(DataSel));  // open: in7
  Comparator #(.mode("unsigned"), .width(2)) comparator_5 (.a(MemAddress[1:0]), .b(2'b00), .eq(bot_0));  // open: gt, lt
  Comparator #(.mode("unsigned"), .width(2)) comparator_6 (.a(MemAddress[1:0]), .b(2'b01), .eq(bot_1));  // open: gt, lt
  Comparator #(.mode("unsigned"), .width(2)) comparator_7 (.a(MemAddress[1:0]), .b(2'b10), .eq(bot_2));  // open: gt, lt
  Comparator #(.mode("unsigned"), .width(2)) comparator_8 (.a(MemAddress[1:0]), .b(2'b11), .eq(bot_3));  // open: gt, lt
  and and_1 (sb_0, op_23, f3_0, bot_0);
  and and_2 (sb_1, op_23, f3_0, bot_1);
  and and_3 (sb_2, op_23, f3_0, bot_2);
  and and_4 (sb_3, op_23, f3_0, bot_3);
  Multiplexer #(.select(3), .width(4)) multiplexer_2 (
    .in0(4'b0001), .in1(4'b0010), .in2(4'b0100), .in3(4'b1000), .in4(4'b0011), .in5(4'b1100), .in6(4'b1111),
    .out(MemWriteMask), .sel(DataSel));  // open: in7
  and and_5 (sh_0, op_23, f3_1, bot_0);
  and and_6 (sh_1, op_23, f3_1, bot_2);
  and and_7 (sw, op_23, f3_2);
  // also tied to GND on the sheet: {DataFromReg[0], DataFromReg[1], DataFromReg[2], DataFromReg[3], DataFromReg[4], DataFromReg[5], DataFromReg[6], DataFromReg[7], DataFromReg[8], DataFromReg[9], DataFromReg[10], DataFromReg[11], DataFromReg[12], DataFromReg[13], DataFromReg[14], DataFromReg[15]}

  // Other names for the same wires on the sheet: data_0[7:0] = DataFromReg[7:0]; data_b[7:0] = DataFromReg[7:0];
  //   data_b_0[7:0] = DataFromReg[7:0]; data_b_1[15:8] = DataFromReg[7:0]; data_b_2[23:16] = DataFromReg[7:0];
  //   data_b_3[31:24] = DataFromReg[7:0]; data_h[15:0] = DataFromReg[15:0];
  //   data_h_0[31:0] = {DataFromReg[15:0], DataFromReg[15:0]}; data_w[31:0] = DataFromReg;
  //   data_1[7:0] = DataFromReg[15:8]; data_2[7:0] = DataFromReg[23:16]; data_3[7:0] = DataFromReg[31:24];
  //   opcode[6:0] = Instruction[6:0]; funct3[2:0] = Instruction[14:12]; funct7[6:0] = Instruction[31:25];
  //   BOT[1:0] = MemAddress[1:0]

  // Notes on the sheet:
  //   INPUTS to your circuit
  //   DON'T CHANGE THE LOCATIONS OF THE INPUTS AND OUTPUTS!
  //   OUTPUT from your circuit
endmodule
